# Fritzing sketch OutdoorStation (saved by Fritzing 0.9.3b)
breadboards: 1

parts:
  Part1 = Arduino Pro Mini v13
  Part2 = NRF24L01+ Breakout Board
  R1 = PHOTOCELL [package=photocell-kit]
  R2 = Resistor [tolerance=±5% resistance=4.7k package=THT]
  VCC1 = Battery

nets:
  GND: Part1.GND, Part2.GND, VCC1.-
  VCC: Part1.VCC, Part2.VCC, R1.P$1, R2.Pin_1, VCC1.+
  N1: Part1.A0, R1.P$2, R2.Pin_0
  N2: Part1.D13/SCK, Part2.SCK
  N3: Part1.D12/MISO, Part2.MISO
  N4: Part1.D11_PWM/MOSI, Part2.MOSI
  N5: Part1.D10_PWM/SS, Part2.CS
  N6: Part1.D9_PWM, Part2.CE
